# Fritzing sketch raspi_bulb (saved by Fritzing 0.9.3b)

parts:
  Raspberry_Pi1 = Raspberry Pi B rev2
  KY-1 = Keyes Relay [package=THT]
  LED5 = LEDs [package=led10mm]
  Power_plug1 = Power plug

nets:
  N1: Raspberry_Pi1.5V, KY-1.power
  N2: Raspberry_Pi1.GND, KY-1.ground
  N3: Raspberry_Pi1.GPIO_17, KY-1.signal
  N4: KY-1.C, Power_plug1.GND
  N5: KY-1.NO, LED5.C
  N6: LED5.A, Power_plug1.VCC

custom parts:
  Keyes Relay: The Keyes 5V relay module is suitable for SCM development, home appliance control. It uses a 5V~12V TIL control signal which can control DC / AC signal.
  LEDs: LEDs Standard schematic elements and footprints for 5mm, 3mm, 1206, and 0603 sized LEDs. 5mm - Spark Fun Electronics SKU : COM-00529 (and others)
